# Fritzing sketch cooker (saved by Fritzing 0.8.5b)
circuit board: 13.3865cm x 11.4232cm
breadboards: 1

parts:
  LCD1 = LCD screen
  R1 = Rotary Potentiometer (Small) [maximum_resistance=100kΩ package=THT]
  R2 = Resistor [tolerance=±5% resistance=1k package=THT]
  R3 = Resistor [tolerance=±5% resistance=1k package=THT]
  R4 = Resistor [tolerance=±5% resistance=1k package=THT]
  3V3 = Battery
  ESP-01 = ESP8266 WiFi Module [part_number=ESP8266]
  BT1 = Bluetooth HC-06u [package=THT]
  R5 = Resistor [tolerance=±5% resistance=1k package=THT]
  R6 = Resistor [tolerance=±5% resistance=1k package=THT]
  R7 = Resistor [tolerance=±5% resistance=1k package=THT]
  R8 = Resistor [tolerance=±5% resistance=10k package=THT]
  Part2 = KY-019 5V Relay Module [package="Breakout board"]
  XTAL1 = Crystal [frequency="16 Mhz" package=THT]
  ATMEGA328 = mystery part, 28 pins [chip_label=Atmega328]
  ROTARY_ENCODER = mystery part, 5 pins [chip_label=KY-040]
  C1 = Tantalum Capacitor [capacitance=20pF package="100 mil [THT, tantalum]"]
  R9 = Resistor [tolerance=±5% resistance=10k package=THT]
  C2 = Tantalum Capacitor [capacitance=20pF package="100 mil [THT, tantalum]"]

nets (from the schematic view):
  VSS: LCD1.VSS, LCD1.LED-, R1.leg2, R4.Pin_0, BT1.GND, R5.Pin_1, Part2.-, ATMEGA328.pin8, ROTARY_ENCODER.pin5, C1.-, C2.-
  VDD: LCD1.VDD, LCD1.LED+, R1.leg1, BT1.VCC, Part2.+, ATMEGA328.pin7, R9.Pin_1
  N1: LCD1.V0, R1.wiper
  N2: LCD1.RS, ATMEGA328.pin14
  N3: LCD1.R/W, ATMEGA328.pin13
  N4: LCD1.E, ATMEGA328.pin12
  N5: LCD1.DB4, ATMEGA328.pin11
  N6: LCD1.DB5, ATMEGA328.pin6
  N7: LCD1.DB6, ATMEGA328.pin5
  N8: LCD1.DB7, ATMEGA328.pin4
  N9: R2.Pin_0, ATMEGA328.pin3
  N10: R2.Pin_1, R3.Pin_1, ESP-01.RXD
  N11: R3.Pin_0, R4.Pin_1
  N12: 3V3.-, ESP-01.GND
  N13: 3V3.+, ESP-01.VCC, ESP-01.GPIO_0, ESP-01.RST, ESP-01.GPIO_2, ESP-01.CH_PD
  N14: ESP-01.TXD, ATMEGA328.pin2
  N15: BT1.TXD, ATMEGA328.pin28
  N16: BT1.RXD, R6.Pin_0, R7.Pin_1
  N17: R5.Pin_0, R6.Pin_1
  N18: R7.Pin_0, ATMEGA328.pin27
  N19: R8.Pin_0, ATMEGA328.pin19, ROTARY_ENCODER.pin3
  N20: R8.Pin_1, ROTARY_ENCODER.pin4
  N21: Part2.S, ATMEGA328.pin16
  N22: XTAL1.pin_0, ATMEGA328.pin9, C1.+
  N23: XTAL1.pin_1, ATMEGA328.pin10, C2.+
  N24: ATMEGA328.pin1, R9.Pin_0
  N25: ATMEGA328.pin17, ROTARY_ENCODER.pin1
  N26: ATMEGA328.pin18, ROTARY_ENCODER.pin2

custom parts:
  ESP8266 WiFi Module: Generic WiFi Module based on the ESP8266 with onboard PCB antenna and UART communications
  Bluetooth HC-06u: Bluetooth HC-06 - face up, pins down 16.5mm x 37.5mm PCB
  KY-019 5V Relay Module: KY-019 5V Relay module, used to control AC circuits.
